// Logisim project PC - copia.circ as structural Verilog: 1 circuit, main circuit main
module main (
  input  in_1
);

  wire adder_4_cout, and_1_out, and_2_out, and_3_out, and_4_out, and_5_out, and_6_out, and_7_out, and_8_out,
       and_9_out, and_10_out, and_11_out, and_13_out, C_3_out, CLR_out, controlled_buffer_30_out,
       controlled_buffer_33_out, controlled_buffer_37_out, controlled_buffer_38_out, CPU_CLK_out,
       decoder_1_out0, decoder_1_out1, decoder_1_out2, decoder_1_out3, decoder_1_out4, decoder_1_out5,
       decoder_1_out6, decoder_1_out7, decoder_1_out8, decoder_1_out9, decoder_1_out10, decoder_1_out11,
       decoder_1_out12, decoder_1_out13, decoder_1_out14, decoder_1_out15, multiplexer_1_out, N_2_out,
       nor_1_out, nor_2_out, nor_3_out, not_1_out, not_3_out, not_4_out, not_5_out, or_1_out, or_2_out,
       or_3_out, or_4_out, or_5_out, or_6_out, or_7_out, or_8_out, or_9_out, or_10_out, or_12_out, or_13_out,
       or_14_out, or_15_out, pull_resistor_2_node, pull_resistor_5_node, Z_2_out;
  wire [1:0] FLAGS___Z_q;
  wire [2:0] rom_1_data;
  wire [7:0] A_prime_q, A_q, adder_2_out, adder_4_out, and_12_out, B_prime_q, B_q, bit_extender_1_out, C_2_q,
       controlled_buffer_1_out, controlled_buffer_5_out, controlled_buffer_11_out, controlled_buffer_13_out,
       controlled_buffer_39_out, IR__HIGH_LEVEL_q, MAhb_q, MAlb_q, MD_q, MP_q, MP_q_2, not_2_out, or_11_out,
       ram_1_data, rom_3_data, SP_q, xor_1_out;
  wire [7:7] FLAGS___CF_q;
  wire [15:0] adder_1_out, adder_3_out, controlled_buffer_2_out, controlled_buffer_7_out,
       controlled_buffer_8_out, controlled_buffer_14_out, MCR_q, rom_2_data;
  wire [31:0] rom_4_data;

  // Probe on rom_4_data[25]
  // Probe on rom_4_data[2]
  // Probe on rom_4_data[31]
  // Probe on rom_4_data[1]
  // Probe on rom_4_data[4]
  // Probe on rom_3_data[6]
  // Probe on rom_3_data[2]
  // Probe on rom_3_data[3]
  // Probe on rom_3_data[4]
  // Probe on rom_3_data[5]
  // Probe on rom_4_data[8]
  // Probe on rom_4_data[10]
  // Probe on rom_4_data[0]
  // Probe on rom_4_data[0]
  or or_1 (or_1_out, rom_3_data[7], rom_3_data[6], rom_3_data[5], rom_3_data[4], rom_3_data[3], rom_3_data[2], rom_3_data[1], rom_3_data[0]);
  and and_1 (and_1_out, multiplexer_1_out, rom_4_data[25]);
  or or_2 (or_2_out, rom_3_data[6], rom_4_data[4]);
  and and_2 (and_2_out, rom_4_data[5], ~CPU_CLK_out);  // AND_Gate
  assign controlled_buffer_1_out = rom_3_data[5] ? {8{1'b1}} : 8'bz;  // Controlled_Buffer controlled_buffer_1
  or or_3 (or_3_out, rom_3_data[4], rom_3_data[5]);
  Pull_Resistor pull_resistor_1 (.node(controlled_buffer_1_out));
  // Probe on rom_4_data[6]
  // Probe on rom_4_data[9]
  // Probe on rom_4_data[11]
  Register #(.trigger("high")) IR__HIGH_LEVEL (
    .D(ram_1_data), .Q(IR__HIGH_LEVEL_q), .clk(rom_4_data[0]));  // open: en, clr
  not not_1 (not_1_out, rom_4_data[0]);
  Adder #(.width(16)) adder_1 (.a(MCR_q), .b(16'h1), .out(adder_1_out));  // open: cin, cout
  assign controlled_buffer_2_out = not_1_out ? adder_1_out : 16'bz;  // Controlled_Buffer controlled_buffer_2
  Clock CPU_CLK (.out(CPU_CLK_out));
  // Probe on rom_3_data[0]
  or or_4 (or_4_out, and_1_out, rom_4_data[31], rom_4_data[2]);
  and and_3 (and_3_out, or_4_out, ~CPU_CLK_out);  // AND_Gate
  and and_4 (and_4_out, or_2_out, ~CPU_CLK_out);  // AND_Gate
  // Probe on rom_4_data[3]
  Pull_Resistor pull_resistor_2 (.node(pull_resistor_2_node));
  assign pull_resistor_2_node = rom_3_data[4] ? 1'b1 : 1'bz;  // Controlled_Buffer controlled_buffer_3
  Adder adder_2 (.a(controlled_buffer_1_out), .b(SP_q), .out(adder_2_out), .cin(pull_resistor_2_node));  // open: cout
  or or_5 (or_5_out, rom_3_data[2], or_3_out);
  // Probe on rom_4_data[7]
  assign controlled_buffer_2_out = rom_4_data[0] ? rom_2_data : 16'bz;  // Controlled_Buffer controlled_buffer_4
  Adder #(.width(16)) adder_3 (.a({MP_q_2, MP_q}), .b(16'h1), .out(adder_3_out));  // open: cin, cout
  // Probe on rom_3_data[7]
  // Probe on and_2_out
  assign controlled_buffer_5_out = rom_3_data[2] ? controlled_buffer_14_out[7:0] : 8'bz;  // Controlled_Buffer controlled_buffer_5
  assign controlled_buffer_5_out = or_3_out ? adder_2_out : 8'bz;  // Controlled_Buffer controlled_buffer_6
  and and_5 (and_5_out, or_5_out, ~CPU_CLK_out);  // AND_Gate
  assign controlled_buffer_7_out = rom_4_data[6] ? controlled_buffer_14_out : 16'bz;  // Controlled_Buffer controlled_buffer_7
  and and_6 (and_6_out, ~CPU_CLK_out, rom_4_data[9]);  // AND_Gate
  or or_6 (or_6_out, rom_4_data[7], rom_4_data[11]);
  and and_7 (and_7_out, or_6_out, ~CPU_CLK_out);  // AND_Gate
  Register #(.width(16)) MCR (.D(controlled_buffer_2_out), .Q(MCR_q), .clk(CPU_CLK_out), .clr(nor_1_out));  // open: en
  nor nor_1 (nor_1_out, or_1_out, or_7_out);
  or or_7 (or_7_out, rom_4_data[31], rom_4_data[30], rom_4_data[29], rom_4_data[28], rom_4_data[27], rom_4_data[26], rom_4_data[25], rom_4_data[24], rom_4_data[23], rom_4_data[22], rom_4_data[21], rom_4_data[20], rom_4_data[19], rom_4_data[18], rom_4_data[17], rom_4_data[16], rom_4_data[15], rom_4_data[14], rom_4_data[13], rom_4_data[12], rom_4_data[11], rom_4_data[10], rom_4_data[9], rom_4_data[8], rom_4_data[7], rom_4_data[6], rom_4_data[5], rom_4_data[4], rom_4_data[3], rom_4_data[2], rom_4_data[1], rom_4_data[0]);
  ROM #(.dataWidth(3)) rom_1 (.addr(IR__HIGH_LEVEL_q), .data(rom_1_data));  // open: sel
  assign controlled_buffer_8_out = and_1_out ? controlled_buffer_14_out : 16'bz;  // Controlled_Buffer controlled_buffer_8
  assign controlled_buffer_8_out = rom_4_data[31] ? controlled_buffer_14_out : 16'bz;  // Controlled_Buffer controlled_buffer_9
  assign controlled_buffer_8_out = rom_4_data[2] ? adder_3_out : 16'bz;  // Controlled_Buffer controlled_buffer_10
  assign controlled_buffer_11_out = rom_4_data[4] ? controlled_buffer_14_out[7:0] : 8'bz;  // Controlled_Buffer controlled_buffer_11
  assign controlled_buffer_11_out = rom_3_data[6] ? controlled_buffer_14_out[15:8] : 8'bz;  // Controlled_Buffer controlled_buffer_12
  Register SP (.D(controlled_buffer_5_out), .Q(SP_q), .clk(and_5_out));  // open: en, clr
  Button CLR (.out(CLR_out));
  nor nor_2 (nor_2_out, rom_4_data[9], rom_4_data[8]);
  Register MD (.D(controlled_buffer_13_out), .Q(MD_q), .clk(and_7_out));  // open: en, clr
  assign controlled_buffer_13_out = rom_4_data[11] ? controlled_buffer_14_out[7:0] : 8'bz;  // Controlled_Buffer controlled_buffer_13
  // Probe on 1'b0
  Multiplexer #(.select(3), .enable("false")) multiplexer_1 (
    .in0(1'b0), .in1(1'b1), .in2(FLAGS___Z_q[0]), .in3(not_5_out), .in4(FLAGS___Z_q[1]), .in5(not_4_out),
    .in6(FLAGS___CF_q[7]), .in7(not_3_out), .out(multiplexer_1_out), .sel(rom_1_data));
  Register #(.width(16)) MP (.D(controlled_buffer_8_out), .Q({MP_q_2, MP_q}), .clk(and_3_out));  // open: en, clr
  Register MAhb (.D(controlled_buffer_11_out), .Q(MAhb_q), .clk(and_4_out));  // open: en, clr
  Register MAlb (.D(controlled_buffer_14_out[7:0]), .Q(MAlb_q), .clk(and_2_out));  // open: en, clr
  assign controlled_buffer_14_out[7:0] = rom_3_data[3] ? SP_q : 8'bz;  // Controlled_Buffer controlled_buffer_14
  RAM #(.addrWidth(16)) ram_1 (
    .addr(controlled_buffer_7_out), .data(ram_1_data), .clk(and_6_out), .ld(nor_2_out), .clr(CLR_out));  // open: sel
  assign ram_1_data = rom_4_data[8] ? MD_q : 8'bz;  // Controlled_Buffer controlled_buffer_15
  assign controlled_buffer_13_out = rom_4_data[7] ? ram_1_data : 8'bz;  // Controlled_Buffer controlled_buffer_16
  assign controlled_buffer_14_out[7:0] = rom_4_data[10] ? MD_q : 8'bz;  // Controlled_Buffer controlled_buffer_17
  ROM #(.dataWidth(16)) rom_2 (.addr(ram_1_data), .data(rom_2_data));  // open: sel
  ROM #(.addrWidth(16)) rom_3 (.addr(MCR_q), .data(rom_3_data));  // open: sel
  ROM #(.addrWidth(16), .dataWidth(32)) rom_4 (.addr(MCR_q), .data(rom_4_data));  // open: sel
  // Probe on controlled_buffer_14_out[15:8]
  // Probe on 1'b1
  assign controlled_buffer_14_out[7:0] = rom_4_data[1] ? MP_q : 8'bz;  // Controlled_Buffer controlled_buffer_18
  assign controlled_buffer_14_out[15:8] = rom_4_data[1] ? MP_q_2 : 8'bz;  // Controlled_Buffer controlled_buffer_19
  assign controlled_buffer_14_out[7:0] = rom_3_data[7] ? MAhb_q : 8'bz;  // Controlled_Buffer controlled_buffer_20
  assign controlled_buffer_14_out[15:8] = rom_4_data[3] ? MAhb_q : 8'bz;  // Controlled_Buffer controlled_buffer_21
  assign controlled_buffer_14_out[7:0] = rom_4_data[3] ? MAlb_q : 8'bz;  // Controlled_Buffer controlled_buffer_22
  Pull_Resistor pull_resistor_3 (.node(controlled_buffer_14_out[15:8]));
  Pull_Resistor pull_resistor_4 (.node(controlled_buffer_14_out[7:0]));
  assign bit_extender_1_out = {{5{1'b0}}, {FLAGS___CF_q[7], FLAGS___Z_q}};  // Bit_Extender bit_extender_1
  assign controlled_buffer_14_out[7:0] = rom_3_data[0] ? bit_extender_1_out : 8'bz;  // Controlled_Buffer controlled_buffer_23
  // Probe on controlled_buffer_14_out[7:0]
  // Probe on FLAGS___Z_q[0]
  assign controlled_buffer_14_out[7:0] = rom_4_data[13] ? A_q : 8'bz;  // Controlled_Buffer controlled_buffer_24
  assign controlled_buffer_14_out[7:0] = rom_4_data[15] ? B_q : 8'bz;  // Controlled_Buffer controlled_buffer_25
  assign controlled_buffer_14_out[7:0] = rom_4_data[17] ? C_2_q : 8'bz;  // Controlled_Buffer controlled_buffer_26
  Decoder #(.select(4), .enable("false")) decoder_1 (
    .out0(decoder_1_out0), .out1(decoder_1_out1), .out2(decoder_1_out2), .out3(decoder_1_out3),
    .out4(decoder_1_out4), .out5(decoder_1_out5), .out6(decoder_1_out6), .out7(decoder_1_out7),
    .out8(decoder_1_out8), .out9(decoder_1_out9), .out10(decoder_1_out10), .out11(decoder_1_out11),
    .out12(decoder_1_out12), .out13(decoder_1_out13), .out14(decoder_1_out14), .out15(decoder_1_out15),
    .sel(rom_4_data[23:20]));
  // Probe on FLAGS___CF_q[7]
  or or_8 (or_8_out, rom_4_data[23], rom_4_data[22], rom_4_data[21], rom_4_data[20]);
  // Probe on not_5_out
  // Probe on FLAGS___Z_q[1]
  // Probe on not_4_out
  // Probe on not_3_out
  // Probe on FLAGS___CF_q[7]
  Register A (.D(controlled_buffer_14_out[7:0]), .Q(A_q), .clk(and_9_out));  // open: en, clr
  Register B (.D(controlled_buffer_14_out[7:0]), .Q(B_q), .clk(and_10_out));  // open: en, clr
  Register C_2 (.D(controlled_buffer_14_out[7:0]), .Q(C_2_q), .clk(and_11_out));  // open: en, clr
  Register A_prime (.D(controlled_buffer_14_out[7:0]), .Q(A_prime_q), .clk(and_8_out));  // open: en, clr
  nor nor_3 (nor_3_out, controlled_buffer_14_out[7], controlled_buffer_14_out[6], controlled_buffer_14_out[5], controlled_buffer_14_out[4], controlled_buffer_14_out[3], controlled_buffer_14_out[2], controlled_buffer_14_out[1], controlled_buffer_14_out[0]);
  and and_8 (and_8_out, ~CPU_CLK_out, rom_4_data[18]);  // AND_Gate
  or or_9 (or_9_out, decoder_1_out1, decoder_1_out2);
  // Probe on controlled_buffer_14_out[7:0]
  Pull_Resistor pull_resistor_5 (.node(pull_resistor_5_node));
  assign pull_resistor_5_node = rom_3_data[1] ? controlled_buffer_14_out[2] : 1'bz;  // Controlled_Buffer controlled_buffer_27
  assign pull_resistor_5_node = or_8_out ? controlled_buffer_37_out : 1'bz;  // Controlled_Buffer controlled_buffer_28
  assign pull_resistor_5_node = rom_4_data[30] ? 1'b1 : 1'bz;  // Controlled_Buffer controlled_buffer_29
  assign controlled_buffer_30_out = rom_3_data[1] ? controlled_buffer_14_out[1] : 1'bz;  // Controlled_Buffer controlled_buffer_30
  assign controlled_buffer_30_out = or_8_out ? controlled_buffer_14_out[7] : 1'bz;  // Controlled_Buffer controlled_buffer_31
  assign controlled_buffer_30_out = rom_4_data[29] ? 1'b1 : 1'bz;  // Controlled_Buffer controlled_buffer_32
  Pull_Resistor pull_resistor_6 (.node(controlled_buffer_30_out));
  assign controlled_buffer_33_out = rom_3_data[1] ? controlled_buffer_14_out[0] : 1'bz;  // Controlled_Buffer controlled_buffer_33
  assign controlled_buffer_33_out = or_8_out ? nor_3_out : 1'bz;  // Controlled_Buffer controlled_buffer_34
  Pull_Resistor pull_resistor_7 (.node(controlled_buffer_33_out));
  assign controlled_buffer_33_out = rom_4_data[28] ? 1'b1 : 1'bz;  // Controlled_Buffer controlled_buffer_35
  and and_9 (and_9_out, ~CPU_CLK_out, rom_4_data[12]);  // AND_Gate
  and and_10 (and_10_out, ~CPU_CLK_out, rom_4_data[14]);  // AND_Gate
  and and_11 (and_11_out, ~CPU_CLK_out, rom_4_data[16]);  // AND_Gate
  Register B_prime (.D(controlled_buffer_14_out[7:0]), .Q(B_prime_q), .clk(and_13_out));  // open: en, clr
  assign controlled_buffer_14_out[7:0] = decoder_1_out14 ? A_prime_q : 8'bz;  // Controlled_Buffer controlled_buffer_36
  assign controlled_buffer_37_out = decoder_1_out14 ? FLAGS___CF_q[7] : 1'bz;  // Controlled_Buffer controlled_buffer_37
  assign controlled_buffer_38_out = decoder_1_out3 ? 1'b1 : 1'bz;  // Controlled_Buffer controlled_buffer_38
  assign controlled_buffer_39_out = or_9_out ? B_prime_q : 8'bz;  // Controlled_Buffer controlled_buffer_39
  assign and_12_out = A_prime_q & B_prime_q;  // AND_Gate and_12, 8 bits wide
  assign not_2_out = ~A_prime_q;  // NOT_Gate not_2, 8 bits wide
  assign controlled_buffer_14_out[7:0] = decoder_1_out5 ? and_12_out : 8'bz;  // Controlled_Buffer controlled_buffer_40
  assign controlled_buffer_14_out[7:0] = decoder_1_out4 ? not_2_out : 8'bz;  // Controlled_Buffer controlled_buffer_41
  Register #(.width(1)) FLAGS___CF (
    .D(pull_resistor_5_node), .Q(FLAGS___CF_q[7]), .clk(C_3_out), .clr(rom_4_data[24]));  // open: en
  Register #(.width(1)) FLAGS___N (
    .D(controlled_buffer_30_out), .Q(FLAGS___Z_q[1]), .clk(N_2_out), .clr(rom_4_data[27]));  // open: en
  Register #(.width(1)) FLAGS___Z (
    .D(controlled_buffer_33_out), .Q(FLAGS___Z_q[0]), .clk(Z_2_out), .clr(rom_4_data[26]));  // open: en
  not not_3 (not_3_out, FLAGS___CF_q[7]);
  not not_4 (not_4_out, FLAGS___Z_q[1]);
  // Probe on rom_4_data[18]
  and and_13 (and_13_out, ~CPU_CLK_out, rom_4_data[19]);  // AND_Gate
  assign controlled_buffer_38_out = decoder_1_out2 ? FLAGS___CF_q[7] : 1'bz;  // Controlled_Buffer controlled_buffer_42
  Pull_Resistor pull_resistor_8 (.node(controlled_buffer_38_out));
  or or_10 (or_10_out, decoder_1_out3, decoder_1_out2, decoder_1_out1);
  Adder adder_4 (
    .a(A_prime_q), .b(controlled_buffer_39_out), .out(adder_4_out), .cin(controlled_buffer_38_out),
    .cout(adder_4_cout));
  Pull_Resistor pull_resistor_9 (.node(controlled_buffer_39_out));
  assign or_11_out = A_prime_q | B_prime_q;  // OR_Gate or_11, 8 bits wide
  assign xor_1_out = A_prime_q ^ B_prime_q;  // XOR_Gate xor_1, 8 bits wide
  assign controlled_buffer_14_out[7:0] = decoder_1_out7 ? xor_1_out : 8'bz;  // Controlled_Buffer controlled_buffer_43
  assign controlled_buffer_14_out[7:0] = decoder_1_out6 ? or_11_out : 8'bz;  // Controlled_Buffer controlled_buffer_44
  // Probe on controlled_buffer_37_out
  not not_5 (not_5_out, FLAGS___Z_q[0]);
  // Probe on rom_4_data[12]
  // Probe on rom_4_data[14]
  // Probe on rom_4_data[16]
  // Probe on rom_4_data[19]
  assign controlled_buffer_14_out[7:0] = or_10_out ? adder_4_out : 8'bz;  // Controlled_Buffer controlled_buffer_45
  assign controlled_buffer_37_out = or_10_out ? adder_4_cout : 1'bz;  // Controlled_Buffer controlled_buffer_46
  or or_12 (or_12_out, decoder_1_out4, decoder_1_out5, decoder_1_out6, decoder_1_out7);
  assign controlled_buffer_37_out = decoder_1_out8 ? A_prime_q[0] : 1'bz;  // Controlled_Buffer controlled_buffer_47
  assign controlled_buffer_14_out[7:0] = decoder_1_out8 ? {1'b0, A_prime_q[7:1]} : 8'bz;  // Controlled_Buffer controlled_buffer_48
  assign controlled_buffer_37_out = decoder_1_out9 ? A_prime_q[0] : 1'bz;  // Controlled_Buffer controlled_buffer_49
  assign controlled_buffer_14_out[7:0] = decoder_1_out9 ? {FLAGS___CF_q[7], A_prime_q[7:1]} : 8'bz;  // Controlled_Buffer controlled_buffer_50
  assign controlled_buffer_14_out[7:0] = decoder_1_out10 ? {A_prime_q[6:0], 1'b0} : 8'bz;  // Controlled_Buffer controlled_buffer_51
  assign controlled_buffer_37_out = decoder_1_out10 ? A_prime_q[7] : 1'bz;  // Controlled_Buffer controlled_buffer_52
  assign controlled_buffer_14_out[7:0] = decoder_1_out11 ? {A_prime_q[6:0], FLAGS___CF_q[7]} : 8'bz;  // Controlled_Buffer controlled_buffer_53
  assign controlled_buffer_37_out = decoder_1_out11 ? A_prime_q[7] : 1'bz;  // Controlled_Buffer controlled_buffer_54
  assign controlled_buffer_14_out[7:0] = decoder_1_out12 ? {A_prime_q[0], A_prime_q[7:1]} : 8'bz;  // Controlled_Buffer controlled_buffer_55
  assign controlled_buffer_37_out = decoder_1_out12 ? FLAGS___CF_q[7] : 1'bz;  // Controlled_Buffer controlled_buffer_56
  assign controlled_buffer_14_out[7:0] = decoder_1_out13 ? {A_prime_q[6:0], A_prime_q[7]} : 8'bz;  // Controlled_Buffer controlled_buffer_57
  assign controlled_buffer_37_out = decoder_1_out13 ? FLAGS___CF_q[7] : 1'bz;  // Controlled_Buffer controlled_buffer_58
  // Probe on rom_3_data[1]
  // Probe on rom_4_data[27]
  // Probe on rom_4_data[26]
  // Probe on rom_4_data[24]
  and C_3 (C_3_out, ~CPU_CLK_out, or_13_out);  // AND_Gate
  or or_13 (or_13_out, rom_4_data[30], rom_3_data[1], or_8_out);
  and N_2 (N_2_out, ~CPU_CLK_out, or_14_out);  // AND_Gate
  or or_14 (or_14_out, rom_4_data[29], rom_3_data[1], or_8_out);
  and Z_2 (Z_2_out, ~CPU_CLK_out, or_15_out);  // AND_Gate
  or or_15 (or_15_out, rom_4_data[28], rom_3_data[1], or_8_out);
  // Probe on rom_4_data[13]
  // Probe on rom_4_data[15]
  // Probe on rom_4_data[17]
  // Probe on rom_4_data[23:20]
  assign controlled_buffer_37_out = or_12_out ? FLAGS___CF_q[7] : 1'bz;  // Controlled_Buffer controlled_buffer_59
  // Probe on rom_4_data[30]
  // Probe on rom_4_data[29]
  Pull_Resistor pull_resistor_10 (.node(controlled_buffer_37_out));
  // Probe on rom_4_data[28]

  // Notes on the sheet:
  //   MP JMP ROM
  //   contents of rom_1 (hex, n*v repeats v):
  //   50*0 1 2 3 4 5 6 7
  //   RAM
  //   MC JMP ROM
  //   MC ROM
  //   contents of rom_2 (hex, n*v repeats v):
  //   1 3 7 b f 17 1f 27 2f 37 3f 41 43 45 47 49 4b 4f 54 5d 61 66 6f 72 75 78 7b 7f 89 8d 92 9b 9f a4 ad
  //   b1 b6 bf c2 cb ce d7 da e3 e6 ef f2 fb fe 107 109 110 117 11e 125 12c 133 13a 13c 13e 140 142 144
  //   157 165 169 16c 16f 172 177
  //   contents of rom_3 (hex, n*v repeats v):
  //   324*0 10 8 10 8 10 8 11 8 40 90 8 10 8 6*0 8 20 8 20 0 8 22 8 20 8 20 8 20 0 0 0 4
  //   contents of rom_4 (hex, n*v repeats v):
  //   43 4 0 4 c2 1404 0 4 c2 4404 0 4 c2 10404 0 4 c2 414 c2 424 c8 1400 0 4 c2 414 c2 424 c8 4400 0 4 c2
  //   414 c2 424 c8 10400 0 4 c2 414 c2 424 2800 348 0 4 c2 414 c2 424 8800 348 0 4 c2 414 c2 424 20800
  //   348 0 6004 0 12004 0 9004 0 18004 0 21004 0 24004 0 42004 88000 101000 0 42004 c2 80404 101000 0
  //   42004 c2 414 c2 424 c8 80400 101000 0 42004 88000 201000 0 42004 c2 80404 201000 0 42004 c2 414 c2
  //   424 c8 80400 201000 0 42004 301000 0 48004 304000 0 60004 310000 0 42004 401000 0 42004 440000
  //   301000 0 4 c2 414 c2 424 c8 40400 440000 301000 0 42004 88000 501000 0 42004 c2 80404 501000 0 42004
  //   c2 414 c2 424 c8 80400 501000 0 42004 88000 601000 0 42004 c2 80404 601000 0 42004 c2 414 c2 424 c8
  //   80400 601000 0 42004 88000 701000 0 42004 c2 80404 701000 0 42004 c2 414 c2 424 c8 80400 701000 0
  //   42004 801000 0 4 c2 414 c2 424 c8 40400 801000 0 42004 901000 0 4 c2 414 c2 424 c8 40400 901000 0
  //   42004 a01000 0 4 c2 414 c2 424 c8 40400 a01000 0 42004 b01000 0 4 c2 414 c2 424 c8 40400 b01000 0
  //   42004 c01000 0 4 c2 414 c2 424 c8 40400 c01000 0 42004 d01000 0 4 c2 414 c2 424 c8 40400 d01000 0
  //   1000004 0 4 c2 414 c2 424 2000008 0 4 c2 414 c2 424 2000008 0 4 c2 414 c2 424 2000008 0 4 c2 414 c2
  //   424 2000008 0 4 c2 414 c2 424 2000008 0 4 c2 414 c2 424 2000008 0 4 c2 414 c2 424 2000008 0 4000004
  //   0 8000004 0 10000004 0 20000004 0 40000004 0 2804 340 8800 340 20800 340 800 340 22 800 340 808 340
  //   c2 414 c2 424 80000008 0 c0 420 c0 410 80000008 c4 404 c0 10400 c0 4400 c0 1400 0 4 c2 404 0 42004
  //   e00000 0 48004 e00000 0 60004 e00000 0 8014 20020 c8 1400 0 8014 20020 2800 348
endmodule
